# Fritzing sketch IRWiFi (saved by Fritzing 0.9.3b)
circuit board: 4.42501cm x 3.63071cm
breadboards: 1

parts:
  R1 = Resistor [tolerance=±5% resistance=100 package=THT]
  LED1 = LED - 5mm [color="Infrared (940nm)" package="5 mm [THT]"]
  LED2 = LED - 5mm [color="Infrared (940nm)" package="5 mm [THT]"]
  R6 = Resistor [tolerance=±5% resistance=100 package=THT]
  R7 = Resistor [tolerance=±5% resistance=100 package=THT]
  IC2 = IC, SIP package, 3 pins [chip_label=ir_rcv]
  IC3 = IC, DIP package, 20 pins [chip_label=WROOM02]
  C1 = Electrolytic Capacitor [capacitance=1µF package="100 mil [THT, electrolytic]"]
  Q1 = NPN-Transistor [package="TO92 [THT]"]
  R3 = Resistor [tolerance=±5% resistance=100 package=THT]
  R2 = Resistor [tolerance=±5% resistance=100 package=THT]
  R4 = Resistor [tolerance=±5% resistance=100 package=THT]
  R5 = Resistor [tolerance=±5% resistance=100 package=THT]

nets:
  N1: R1.Pin_0, IC3.pin12
  N2: R1.Pin_1, Q1.B
  N3: LED1.cathode, R3.Pin_0, R2.Pin_0, R4.Pin_0, R5.Pin_0
  N4: LED1.anode, LED2.cathode
  5V: LED2.anode, IC3.pin10
  N5: R6.Pin_0, R7.Pin_0, IC2.pin3, C1.+
  3.3V: R6.Pin_1, R7.Pin_1, IC3.pin1
  N6: IC2.pin1, IC3.pin3
  GND: IC2.pin2, IC3.pin9, IC3.pin15, IC3.pin20, C1.-, Q1.E
  N7: Q1.C, R3.Pin_1, R2.Pin_1, R4.Pin_1, R5.Pin_1
